# Fritzing sketch Sensor de linea (saved by Fritzing 0.9.2b)
breadboards: 1

parts:
  Op1 = LMV324 [package=so014]
  R2 = TRIMPOT [package=trim_pot_pth]
  J1 = male pin header, 10 pins [form="♂ (male)"]
  Op2 = LMV324 [package=so014]
  pT1 = LTR-301 [package=ltr-301]
  R3 = Resistor [tolerance=±5% resistance=220 package=THT]
  pT2 = LTR-301 [package=ltr-301]
  R4 = Resistor [tolerance=±5% resistance=220 package=THT]
  pT3 = LTR-301 [package=ltr-301]
  R5 = Resistor [tolerance=±5% resistance=220 package=THT]
  pT4 = LTR-301 [package=ltr-301]
  R6 = Resistor [tolerance=±5% resistance=220 package=THT]
  pT5 = LTR-301 [package=ltr-301]
  R7 = Resistor [tolerance=±5% resistance=220 package=THT]
  pT6 = LTR-301 [package=ltr-301]
  R8 = Resistor [tolerance=±5% resistance=220 package=THT]
  pT7 = LTR-301 [package=ltr-301]
  R9 = Resistor [tolerance=±5% resistance=220 package=THT]
  pT8 = LTR-301 [package=ltr-301]
  R10 = Resistor [tolerance=±5% resistance=220 package=THT]

nets:
  p1: Op1.G$1_OUT, J1.pin1
  vPot: Op1.G$1_-IN, Op1.G$2_-IN, Op1.G$3_-IN, Op1.G$4_-IN, R2.WIPER, Op2.G$1_-IN, Op2.G$2_-IN, Op2.G$3_-IN, Op2.G$4_-IN
  vpT1: Op1.G$1_+IN, pT1.C, R3.Pin_1
  5V: Op1.G$1_+V, R2.CCW, J1.pin9, R3.Pin_0, R4.Pin_0, R5.Pin_0, R6.Pin_0, R7.Pin_0, R8.Pin_0, R9.Pin_0, R10.Pin_0
  vpT2: Op1.G$2_+IN, pT2.C, R4.Pin_1
  p2: Op1.G$2_OUT, J1.pin2
  p3: Op1.G$3_OUT, J1.pin3
  vpT3: Op1.G$3_+IN, pT3.C, R5.Pin_1
  GND: Op1.G$1_-V, R2.CW, J1.pin10, pT1.E, pT2.E, pT3.E, pT4.E, pT5.E, pT6.E, pT7.E, pT8.E
  vpT4: Op1.G$4_+IN, pT4.C, R6.Pin_1
  p4: Op1.G$4_OUT, J1.pin4
  p5: J1.pin5, Op2.G$1_OUT
  p6: J1.pin6, Op2.G$2_OUT
  p7: J1.pin7, Op2.G$3_OUT
  p8: J1.pin8, Op2.G$4_OUT
  vpT5: Op2.G$1_+IN, pT5.C, R7.Pin_1
  vpT6: Op2.G$2_+IN, pT6.C, R8.Pin_1
  vpT7: Op2.G$3_+IN, pT7.C, R9.Pin_1
  vpT8: Op2.G$4_+IN, pT8.C, R10.Pin_1
